# Fritzing sketch Schema-electronique (saved by Fritzing 1.0.6)
breadboards: 1

parts:
  Composant2 = Quarter 60 NeoPixel Ring [part_number=1768]
  Composant3 = Quarter 60 NeoPixel Ring [part_number=1768]
  Composant4 = Quarter 60 NeoPixel Ring [part_number=1768]
  Composant5 = Quarter 60 NeoPixel Ring [part_number=1768]
  Composant6 = Arduino Uno (Rev3)
  Composant7 = Adafruit DS1307 RTC Breakout [part_number="Adafruit #264"]
  Composant8 = 14-segment LED Alphanumeric Backpack [part_number=2160]
  S1 = Momentary Switch [package=ksa_sealed_tac_switch]
  S2 = Momentary Switch [package=ksa_sealed_tac_switch]
  S3 = Momentary Switch [package=ksa_sealed_tac_switch]
  S4 = Momentary Switch [package=ksa_sealed_tac_switch]
  S5 = Momentary Switch [package=ksa_sealed_tac_switch]
  S6 = Momentary Switch [package=ksa_sealed_tac_switch]
  Composant9 = Adafruit BME680

nets:
  VDD: Composant2.VDD, Composant3.VDD, Composant4.VDD, Composant5.VDD, Composant6.5V, Composant7.VCC, Composant8.VDD, Composant9.3.3V
  N1: Composant2.DATAIN, Composant3.DATAOUT, Composant4.DATAOUT, Composant5.DATAIN
  GND: Composant2.GND, Composant3.GND, Composant4.GND, Composant5.GND, Composant6.GND, Composant7.GND, Composant8.GND, S1.1, S1.3, S2.1, S2.3, S3.1, S3.3, S4.1, S4.3, S5.1, S5.3, S6.1, S6.3, Composant9.GND
  N2: Composant2.DATAOUT, Composant3.DATAIN, Composant5.DATAOUT
  N3: Composant4.DATAIN, Composant6.D6_PWM
  N4: Composant6.A4/SDA, Composant7.SDA, Composant8.SDA, Composant9.SDI/SDA
  N5: Composant6.A5/SCL, Composant7.SCL, Composant8.SCL, Composant9.SCK/SCL
  N6: Composant6.D8, S1.2
  N7: Composant6.D2, S5.2
  N8: Composant6.D3_PWM, S6.2
  N9: Composant6.D4, S4.2
  N10: Composant6.D5_PWM, S3.2
  N11: Composant6.D7, S2.2

custom parts:
  Quarter 60 NeoPixel Ring: The biggest NeoPixel Ring yet! With four of these you can make a huge ring with 60 ultra bright smart LED NeoPixels are arranged in a circle with a 6.2" diameter. The rings are 'chainable' - connect the output pin of one to the input pin of another. Use only one microcontroller pin to control as many as you can chain together!
  Adafruit DS1307 RTC Breakout: This is a great battery-backed real time clock (RTC) that allows your microcontroller project to keep track of time even if it is reprogrammed, or if the power is lost. Perfect for datalogging, clock-building, time stamping, timers and alarms, etc. The DS1307 is the most popular RTC - but it requires 5V power to work (although we've used it with 5V power and 3.3V logic successfully) PCB &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
  14-segment LED Alphanumeric Backpack: This is a nice, bright alphanumeric display that shows letters and numbers. It's super bright and designed for viewing from distances up to 23 feet (7 meters) away. Four digits with 14 segments on a black surface and we give you a set of two alphanumeric displays as well as a driver board so you can make a clock or a four letter word. Like our other LED backpacks, these are end-to-end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
